# Fritzing sketch montaje_driverymotores (saved by Fritzing 0.9.3b)
breadboards: 1

parts:
  Part1 = Motor Driver 1A Dual TB6612FNG  # not connected
  U1 = 74HC04_HEX_INVERTER [package=dil14]
  Part2 = RobotDyn UNO R3 CH340
  VCC1 = 4 x AAA Battery Mount
  M2 = DC Motor  # not connected
  M3 = DC Motor  # not connected

nets:
  N1: U1.1A, Part2.D7
  N2: U1.2A, Part2.D4
  GND: U1.GND, Part2.GND
  VCC: U1.VCC, Part2.5V
  N3: Part2.VIN, VCC1.+

custom parts:
  RobotDyn UNO R3 CH340: Uno R3 CH340G/ATmega328P - compatible with the Arduino Uno R3 board, based on the microcontroller ATmega328P (SMD-version) and USB-UART interface chip CH340G.
